# Fritzing sketch grillsensor-xiaoesp32-c6-b (saved by Fritzing 1.0.8)
circuit board: 2.413cm x 2.032cm
perfboards: 1

parts:
  U1 = XIAO ESP32C6 [part_number=" XIAO ESP32C6"]
  R1 = Resistor [tolerance=±5% power=0.25W resistance=47k package=THT]
  R2 = Resistor [tolerance=±5% power=0.25W resistance=47k package=THT]
  TRS2 = Audio Jack (TRS) 3.5mm [package="4Ucon 08780 [THT]"]
  V1 = DC Power [voltage=5V internal_resistance=0.1Ω]
  C1 = Ceramic Capacitor [capacitance=100nF voltage=35V package="100 mil [THT, multilayer]"]
  R3 = Resistor [tolerance=±5% power=0.25W resistance=1M package=THT]
  R4 = Resistor [tolerance=±5% power=0.25W resistance=1M package=THT]
  C2_-Low-ESR = Electrolytic Capacitor [capacitance=470µF voltage=6.3V package="100 mil [THT, electrolytic]"]
  C2 = Ceramic Capacitor [capacitance=100nF voltage=35V package="100 mil [THT, multilayer]"]
  C3 = Ceramic Capacitor [capacitance=100nF voltage=35V package="100 mil [THT, multilayer]"]
  TRS3 = Audio Jack (TRS) 3.5mm [package="4Ucon 08780 [THT]"]

nets:
  N1: U1.D0, R1.Pin_1, TRS2.Ring, C2.0
  N2: U1.D1, R2.Pin_1, C3.0, TRS3.Ring
  N3: U1.D2, C1.1, R3.Pin_0, R4.Pin_1
  N4: U1.D3, R1.Pin_0, R2.Pin_0
  GND: U1.GND, TRS2.Sleeve, V1.V-, C1.0, R4.Pin_0, C2_-Low-ESR.-, C2.1, C3.1, TRS3.Sleeve
  N5: V1.V+, R3.Pin_1, C2_-Low-ESR.+

custom parts:
  XIAO ESP32C6: XIAO ESP32C6 is a cost-effective MCU based on Espressif’s ESP32-C6. This compact MCU excels in Matter-compliant smart home applications with its support for various wireless connectivity (2.4GHz Wi-Fi 6, BLE 5.0, Zigbee, and Thread). Designed with the thumb-size footprint and a single-sided mount of the XIAO Series, it's perfect for space-limited projects. Encrypted on the chip, the XIAO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
